# Fritzing sketch Weathercube (saved by Fritzing 0.9.3b)
breadboards: 1

parts:
  Часть1 = Arduino Leonardo (Rev3b)
  LED1 = LED - 3mm [color="Green (555nm)" package="3 mm [THT]"]
  LED2 = LED - 3mm [color="Green (555nm)" package="3 mm [THT]"]
  LED3 = LED - 3mm [color="Red (633nm)" package="3 mm [THT]"]
  LED4 = LED - 3mm [color="Red (633nm)" package="3 mm [THT]"]
  R1 = Resistor [tolerance=±5% resistance=220 package="2512 [SMD]"]
  R2 = Resistor [tolerance=±5% resistance=220 package="2512 [SMD]"]
  R3 = Resistor [tolerance=±5% resistance=220 package="2512 [SMD]"]
  R4 = Resistor [tolerance=±5% resistance=220 package="2512 [SMD]"]

nets:
  N1: Часть1.D5_PWM, LED4.anode, R1.Pin_0, R1.Pin_1
  N2: Часть1.D6_PWM/A7, LED1.anode, R3.Pin_0, R3.Pin_1
  N3: Часть1.GND, LED1.cathode, LED3.cathode, LED4.cathode
  N4: Часть1.D9_PWM/A9, LED3.anode, R2.Pin_0, R2.Pin_1
  N5: Часть1.D10_PWM/A10, LED2.anode, R4.Pin_0, R4.Pin_1
